// Logisim project DecodeIR.circ as structural Verilog: 2 circuits, main circuit main
module DecodeIR (
  input  [31:0] IR,
  output WriteReg,
  output Store,
  output Load,
  output CTRL,
  output [2:0] GetOp,
  output [15:0] JMPAddress
);


  assign CTRL = 1'b0;
  assign GetOp = 3'b000;
  assign JMPAddress = {16{1'b0}};
  assign Load = 1'b0;
  assign Store = 1'b0;
  assign WriteReg = 1'b1;
endmodule

module _16_bit_transistor (
  input  [15:0] in_1,
  input  Test,
  output [15:0] Arith
);

  and and_1 (Arith[0], in_1[0], Test);
  and and_2 (Arith[1], in_1[1], Test);
  and and_3 (Arith[2], in_1[2], Test);
  and and_4 (Arith[3], in_1[3], Test);
  and and_5 (Arith[4], in_1[4], Test);
  and and_6 (Arith[5], in_1[5], Test);
  and and_7 (Arith[6], in_1[6], Test);
  and and_8 (Arith[7], in_1[7], Test);
  and and_9 (Arith[8], in_1[8], Test);
  and and_10 (Arith[9], in_1[9], Test);
  and and_11 (Arith[10], in_1[10], Test);
  and and_12 (Arith[11], in_1[11], Test);
  and and_13 (Arith[12], in_1[12], Test);
  and and_14 (Arith[13], in_1[13], Test);
  and and_15 (Arith[14], in_1[14], Test);
  and and_16 (Arith[15], in_1[15], Test);
endmodule
