// Logisim project GetCst.circ as structural Verilog: 1 circuit, main circuit main
module GetCst (
  input  [31:0] IR,
  output [15:0] Cst,
  output Imm
);

  Bit_Extender #(.in_width(20)) bit_extender_1 (.in(IR[31:12]), .out(Cst));

  assign Imm = IR[5];
endmodule
