// Logisim project Main.circ as structural Verilog: 1 circuit, main circuit main
module main (
  input  Reset,
  input  ResetRAM
);

  wire alu_1_p1, alu_1_p3, Clock, Clock_out, CTRL, Exec, Fetch, getcst_1_p2, getcst_1_p3, getcst_1_p7, Load,
       ramctrl_1_p4, ramctrl_1_p5, Store, WriteReg;
  wire [2:0] GetOp;
  wire [15:0] Addr, JMP_Address, MemIN, PC, R0, R1, R2, R3, R4, R5, R6, R7;
  wire [31:0] bit_extender_1_out, IR, MemOUT;

  Clock u_Clock (.out(Clock_out));
  // Seq seq_1: pin names not known; wires that end beside it: Clock_out, Reset, Clock, Fetch, Exec
  LED led_1 (.in(Clock_out));
  // RegPC regpc_1: pin names not known; wires that end beside it: 1'b0, CTRL, Exec, Reset, JMP_Address
  // Probe on PC
  // GetAddr getaddr_1: pin names not known; wires that end beside it: Fetch, Load, Store, PC, PC, Addr
  // Probe on Addr
  LED led_2 (.in(Fetch));
  LED led_3 (.in(Exec));
  // Probe on MemIN
  assign bit_extender_1_out = {{16{MemIN[15]}}, MemIN};  // Bit_Extender bit_extender_1
  // Probe on PC
  // Probe on IR
  // DecodeIR decodeir_1: pin names not known; wires that end beside it: Load, Store, CTRL, GetOp, IR, WriteReg, JMP_Address
  // RamCtrl ramctrl_1: pin names not known; wires that end beside it: Clock, Fetch, Exec, ramctrl_1_p4, ramctrl_1_p5, Load, Store
  // Probe on MemOUT
  RAM #(.addrWidth(16), .dataWidth(32), .bus("separate")) ram_1 (
    .addr(Addr), .din(bit_extender_1_out), .data(MemOUT), .str(ramctrl_1_p4), .clk(ramctrl_1_p4),
    .ld(ramctrl_1_p5), .clr(ResetRAM));  // open: sel
  // Probe on R0
  // Probe on R3
  // Probe on R6
  Register #(.width(32), .trigger("falling")) RegIR (.D(MemOUT), .Q(IR), .clk(Fetch), .clr(Reset));  // open: en
  // Probe on R1
  // Probe on R4
  // Probe on R7
  // Probe on IR
  // Probe on R2
  // Probe on R5
  // Probe on IR[8:6]
  // Probe on IR[11:9]
  // Probe on IR[14:12]
  // Probe on getcst_1_p2
  // GetCst getcst_1: pin names not known; wires that end beside it: IR, getcst_1_p2, getcst_1_p3, getcst_1_p2, getcst_1_p3, GetOp, getcst_1_p7
  // Registres registres_1: pin names not known; wires that end beside it: IR, Exec, IR[14:12], IR[11:9], IR[8:6], WriteReg, getcst_1_p7, Reset, R0, R1, R2, R3, R4, R5, R6, R7
  // Probe on alu_1_p1
  // Probe on alu_1_p3
  // ALU alu_1: pin names not known; wires that end beside it: alu_1_p1, alu_1_p1, alu_1_p3, alu_1_p3, MemIN
  // Probe on getcst_1_p7
  // Probe on R0
  // Probe on R1
  // Probe on R2
  // Probe on R3
  // Probe on R4
  // Probe on R5
  // Probe on R6
  // Probe on R7
  // Probe on getcst_1_p7

  // Notes on the sheet:
  //   RAM
endmodule
