// Logisim project RegPC.circ as structural Verilog: 1 circuit, main circuit main
module RegPC (
  input  [15:0] JMP_Address,
  input  Cond,
  input  CTRL,
  input  Clock,
  input  Reset,
  output [15:0] PC
);

  Register #(.width(16), .trigger("falling")) u_PC (.Q(PC), .clk(Clock), .clr(Reset));  // open: D, en
endmodule
