// Logisim project Registres.circ as structural Verilog: 2 circuits, main circuit Registres
module Registres (
  input  [15:0] IN,
  input  [2:0] SR1,
  input  [2:0] SR2,
  input  [2:0] DR,
  input  WriteReg,
  input  Clock,
  input  Reset,
  output [15:0] R0,
  output [15:0] OUT_SR1,
  output [15:0] R1,
  output [15:0] R2,
  output [15:0] R3,
  output [15:0] OUT_SR2,
  output [15:0] R4,
  output [15:0] R5,
  output [15:0] OUT_DR,
  output [15:0] R6,
  output [15:0] R7
);

  wire demultiplexer_1_out0, demultiplexer_1_out1, demultiplexer_1_out2, demultiplexer_1_out3,
       demultiplexer_1_out4, demultiplexer_1_out5, demultiplexer_1_out6, demultiplexer_1_out7,
       multiplexer_1_out;

  Demultiplexer #(.select(3)) demultiplexer_1 (
    .out0(demultiplexer_1_out0), .out1(demultiplexer_1_out1), .out2(demultiplexer_1_out2),
    .out3(demultiplexer_1_out3), .out4(demultiplexer_1_out4), .out5(demultiplexer_1_out5),
    .out6(demultiplexer_1_out6), .out7(demultiplexer_1_out7), .in(Clock), .sel(DR), .en(WriteReg));
  Register #(.width(16), .trigger("falling")) u_R0 (
    .D(IN), .Q(R0), .clk(demultiplexer_1_out0), .clr(Reset));  // open: en
  Register #(.width(16), .trigger("falling")) u_R1 (
    .D(IN), .Q(R1), .clk(demultiplexer_1_out1), .clr(Reset));  // open: en
  Register #(.width(16), .trigger("falling")) u_R2 (
    .D(IN), .Q(R2), .clk(demultiplexer_1_out2), .clr(Reset));  // open: en
  Register #(.width(16), .trigger("falling")) u_R3 (
    .D(IN), .Q(R3), .clk(demultiplexer_1_out3), .clr(Reset));  // open: en
  Register #(.width(16), .trigger("falling")) u_R4 (
    .D(IN), .Q(R4), .clk(demultiplexer_1_out4), .clr(Reset));  // open: en
  Register #(.width(16), .trigger("falling")) u_R5 (
    .D(IN), .Q(R5), .clk(demultiplexer_1_out5), .clr(Reset));  // open: en
  Register #(.width(16), .trigger("falling")) u_R6 (
    .D(IN), .Q(R6), .clk(demultiplexer_1_out6), .clr(Reset));  // open: en
  Register #(.width(16), .trigger("falling")) u_R7 (
    .D(IN), .Q(R7), .clk(demultiplexer_1_out7), .clr(Reset));  // open: en
  Multiplexer #(.enable("false")) multiplexer_1 (.in0(Clock), .in1(1'b0), .out(multiplexer_1_out), .sel(WriteReg));
  Multiplexer #(.select(3), .width(16)) multiplexer_2 (
    .in0(R0), .in1(R1), .in2(R2), .in3(R3), .in4(R4), .in5(R5), .in6(R6), .in7(R7), .out(OUT_SR1), .sel(SR1),
    .en(Clock));
  Multiplexer #(.select(3), .width(16)) multiplexer_3 (
    .in0(R0), .in1(R1), .in2(R2), .in3(R3), .in4(R4), .in5(R5), .in6(R6), .in7(R7), .out(OUT_SR2), .sel(SR2),
    .en(Clock));
  Multiplexer #(.select(3), .width(16)) multiplexer_4 (
    .in0(R0), .in1(R1), .in2(R2), .in3(R3), .in4(R4), .in5(R5), .in6(R6), .in7(R7), .out(OUT_DR), .sel(DR),
    .en(multiplexer_1_out));
endmodule

module _16_bit_transistor (
  input  [15:0] in_1,
  input  Test,
  output [15:0] Arith
);

  and and_1 (Arith[0], in_1[0], Test);
  and and_2 (Arith[1], in_1[1], Test);
  and and_3 (Arith[2], in_1[2], Test);
  and and_4 (Arith[3], in_1[3], Test);
  and and_5 (Arith[4], in_1[4], Test);
  and and_6 (Arith[5], in_1[5], Test);
  and and_7 (Arith[6], in_1[6], Test);
  and and_8 (Arith[7], in_1[7], Test);
  and and_9 (Arith[8], in_1[8], Test);
  and and_10 (Arith[9], in_1[9], Test);
  and and_11 (Arith[10], in_1[10], Test);
  and and_12 (Arith[11], in_1[11], Test);
  and and_13 (Arith[12], in_1[12], Test);
  and and_14 (Arith[13], in_1[13], Test);
  and and_15 (Arith[14], in_1[14], Test);
  and and_16 (Arith[15], in_1[15], Test);
endmodule
