// Logisim project Total.circ as structural Verilog: 10 circuits, main circuit main
module main (
  input  Reset,
  input  ResetRAM,
  output \Immédiat 
);

  wire Clock, Clock_out, CTRL, decodeir_1_store, Exec, Fetch, Load, or_1_out, ramctrl_1_memload,
       ramctrl_1_memstore, registres_1_p6, registres_1_p8, registres_1_p9, seq_1_fetch, Store, undriven,
       undriven_2, undriven_3, undriven_4, WriteReg;
  wire [2:0] decodeir_1_getop;
  wire [15:0] Addr, addr_store_load, getcst_1_cst_2, JMP_Address, MemIN, PC, R0, R1, R2, R3, R4, R5, R6;
  wire [31:0] bit_extender_1_out, IR, MemOUT;

  Clock u_Clock (.out(Clock_out));
  Seq seq_1 (.ClockOrig(Clock_out), .reset(Reset), .Fetch(seq_1_fetch), .Exec(Clock));
  LED led_1 (.in(Clock_out));
  LED led_2 (.in(Clock_out));
  RegPC regpc_1 (.Cond(undriven), .CTRL_2(CTRL), .Clock_2(Exec), .Reset_2(Reset), .PC(PC));
  // Probe on PC
  GetAddr getaddr_1 (.PC(PC), .Addr(Addr), .Fetch(Fetch), .Store(Load), .Store_2(Exec), .in_2(addr_store_load));
  // Probe on Addr
  LED led_3 (.in(Fetch));
  LED #(.width(3)) GetOp (.in(seq_1_fetch));
  assign bit_extender_1_out = {{16{MemIN[15]}}, MemIN};  // Bit_Extender bit_extender_1
  // Probe on MemIN
  // Probe on PC
  // Probe on IR
  // Probe on IR
  DecodeIR decodeir_1 (
    .CTRL(CTRL), .WriteReg(WriteReg), .IR(IR), .Load(Load), .out_7(JMP_Address), .Store(decodeir_1_store),
    .GetOp(decodeir_1_getop));
  RamCtrl ramctrl_1 (
    .Store_2(Store), .Exec(Fetch), .Load(Load), .MemStore(ramctrl_1_memstore), .MemLoad(ramctrl_1_memload),
    .Clock(Clock));
  // Probe on MemOUT
  RAM #(.addrWidth(16), .dataWidth(32), .bus("separate")) ram_1 (
    .addr(Addr), .din(bit_extender_1_out), .data(MemOUT), .str(ramctrl_1_memstore), .clk(ramctrl_1_memstore),
    .ld(ramctrl_1_memload), .clr(ResetRAM));  // open: sel
  // Probe on undriven_2
  // Probe on R3
  // Probe on R3
  Register #(.width(32), .trigger("falling")) RegIR (.D(MemOUT), .en(undriven_3), .Q(IR), .clk(Fetch), .clr(Reset));
  Register #(.width(32), .trigger("falling")) RegIR_2 (.D(MemOUT), .en(undriven_3), .Q(IR), .clk(Fetch), .clr(Reset));
  // Probe on R1
  // Probe on undriven_4
  // Probe on R5
  // Probe on IR
  // Probe on R2
  // Probe on R5
  or or_1 (or_1_out, Load, Store);
  // Probe on IR[8:6]
  // Probe on IR[11:9]
  // Probe on IR[14:12]
  // Probe on getcst_1_cst_2
  GetCst getcst_1 (.IR_2(IR), .Cst_2(getcst_1_cst_2), .Imm(\Immédiat ));
  // Probe on getcst_1_cst_2
  // Registres registres_1: pin names not known; wires that end beside it: Exec, IR[14:12], IR[11:9], IR[8:6], WriteReg, registres_1_p6, or_1_out, registres_1_p8, registres_1_p9, Reset, MemIN, R0, R1, R2, R3, R4, R5, R6, MemIN
  // Probe on registres_1_p6
  // Probe on registres_1_p9
  // ALU alu_1: pin names not known; wires that end beside it: getcst_1_cst_2, \Immédiat , PC, registres_1_p8
  // Probe on registres_1_p8
  // Probe on R0
  // Probe on R1
  // Probe on R2
  // Probe on R2
  // Probe on R3
  // Probe on R4
  // Probe on R5
  // Probe on R6
  // Probe on MemIN
  // Probe on registres_1_p8

  // Notes on the sheet:
  //   RAM
endmodule

module ALU (
  input  [15:0] Cst,
  input  [15:0] Cst_2,
  input  [2:0] e2,
  input  Imm,
  input  Imm_2,
  input  [2:0] e2_2
);

  wire subtractor_1_bout, undriven_4;
  wire [15:0] adder_1_out, and_1_out, or_1_out, shifter_1_out, shifter_2_out, subtractor_1_out, undriven,
       undriven_2, undriven_3, xor_1_out;
  wire [15:3] multiplexer_1_out;

  Adder #(.width(16)) adder_1 (.a(undriven), .b(undriven_2), .out(adder_1_out));  // open: cin, cout
  Subtractor #(.width(16)) subtractor_1 (
    .a(undriven), .b(undriven_2), .out(subtractor_1_out), .bin(undriven_4), .bout(subtractor_1_bout));
  Subtractor #(.width(16)) subtractor_2 (
    .a(undriven), .b(undriven_2), .out(subtractor_1_out), .bin(undriven_4), .bout(subtractor_1_bout));
  assign and_1_out = undriven & undriven_2;  // AND_Gate and_1, 16 bits wide
  assign and_1_out = undriven & undriven_2 & undriven_3;  // AND_Gate Output, 16 bits wide
  assign or_1_out = undriven_3 | undriven | undriven_2;  // OR_Gate or_1, 16 bits wide
  assign xor_1_out = undriven ^ undriven_2;  // XOR_Gate xor_1, 16 bits wide
  assign xor_1_out = undriven ^ undriven_2;  // XOR_Gate xor_2, 16 bits wide
  Shifter #(.width(16)) shifter_1 (.in(undriven), .\dist (4'b0001), .out(shifter_1_out));
  Shifter #(.width(16), .shift("lr")) shifter_2 (.in(undriven), .\dist (4'b0001), .out(shifter_2_out));
  Multiplexer #(.select(3), .width(16), .enable("false")) multiplexer_1 (
    .out({multiplexer_1_out, e2}), .sel(e2_2));  // open: in0, in1, in2, in3, in4, in5, in6, in7
  // Pins of 3 and 16 bits meet at {multiplexer_1_out, e2}

  assign Cst_2 = Cst;
  assign Imm_2 = Imm;
endmodule

module DecodeIR (
  input  [31:0] IR,
  output WriteReg,
  output Store,
  output Load,
  output CTRL,
  output [2:0] GetOp,
  output [15:0] out_7
);

  Decoder #(.select(2), .enable("false")) decoder_1 (
    .out0(WriteReg), .out1(Store), .out2(Load), .out3(CTRL), .sel(IR[1:0]));
  assign out_7 = CTRL ? IR[31:16] : 16'bz;  // Controlled_Buffer controlled_buffer_1

  assign GetOp = IR[4:2];
endmodule

module GetAddr (
  input  [15:0] PC,
  input  [15:0] in_2,
  input  Store,
  input  Store_2,
  input  Fetch,
  output [15:0] Addr
);

  wire not_1_out, or_1_out;
  wire [15:0] controlled_buffer_1_out;

  or or_1 (or_1_out, Store, Store_2);
  or or_2 (or_1_out, Store, Store_2);
  assign controlled_buffer_1_out = or_1_out ? in_2 : 16'bz;  // Controlled_Buffer controlled_buffer_1
  assign controlled_buffer_1_out = or_1_out ? in_2 : 16'bz;  // Controlled_Buffer controlled_buffer_2
  not not_1 (not_1_out, Fetch);
  not not_2 (not_1_out, Fetch);
  Multiplexer #(.width(16), .enable("false")) multiplexer_1 (
    .in0(PC), .in1(controlled_buffer_1_out), .out(Addr), .sel(not_1_out));
  Multiplexer #(.width(16), .enable("false")) multiplexer_2 (
    .in0(PC), .in1(controlled_buffer_1_out), .out(Addr), .sel(not_1_out));
endmodule

module GetCst (
  input  [31:0] IR,
  input  [31:0] IR_2,
  output [15:0] Cst,
  output [15:0] Cst_2,
  output Imm
);

  Bit_Extender #(.in_width(20)) bit_extender_1 (.in(IR[31:12]), .out(Cst));
  Bit_Extender #(.in_width(20)) bit_extender_2 (.in(IR[31:12]), .out(Cst));
  // Probe on IR[31:12]
  // Probe on IR[31:12]

  assign Cst_2 = Cst;
  assign Imm = IR[5];
  assign IR_2 = IR;
endmodule

module RamCtrl (
  input  Clock,
  input  Exec,
  input  Load,
  input  Store,
  input  Store_2,
  output MemLoad,
  output MemStore
);

  wire and_1_out, undriven;

  and and_1 (and_1_out, undriven, Load);
  and and_2 (MemStore, undriven, Clock, Store);
  and and_3 (MemStore, undriven, Clock, Store);

  assign Store_2 = Store;
endmodule

module Registres (
  input  [15:0] Clock,
  input  [2:0] SR1,
  input  [2:0] SR2,
  input  WriteReg,
  input  WriteReg_2,
  input  Clock_2,
  input  R7,
  input  Reset,
  output [15:0] R0,
  output [15:0] R1,
  output [15:0] R1_2,
  output [15:0] R2,
  output [15:0] R3,
  output [15:0] OUT_SR2,
  output [15:0] R4,
  output [15:0] R0_2,
  output [15:0] R3_2,
  output [15:0] Reset_2,
  output [15:0] R3_3
);

  wire demultiplexer_1_out0, demultiplexer_1_out1, demultiplexer_1_out2, demultiplexer_1_out3,
       demultiplexer_1_out4, demultiplexer_1_out5, demultiplexer_1_out6, demultiplexer_1_out7;
  wire [2:0] DR;

  Demultiplexer #(.select(3)) demultiplexer_1 (
    .out0(demultiplexer_1_out0), .out1(demultiplexer_1_out1), .out2(demultiplexer_1_out2),
    .out3(demultiplexer_1_out3), .out4(demultiplexer_1_out4), .out5(demultiplexer_1_out5),
    .out6(demultiplexer_1_out6), .out7(demultiplexer_1_out7), .in(Clock_2), .sel(DR), .en(WriteReg));
  Register #(.width(16), .trigger("falling")) u_R0 (
    .D(Clock), .Q(R0), .clk(demultiplexer_1_out0), .clr(Reset));  // open: en
  Register #(.width(16), .trigger("falling")) u_R1 (
    .D(Clock), .Q(R1_2), .clk(demultiplexer_1_out1), .clr(Reset));  // open: en
  Register #(.width(16), .trigger("falling")) u_R2 (
    .D(Clock), .Q(R2), .clk(demultiplexer_1_out2), .clr(Reset));  // open: en
  Register #(.width(16), .trigger("falling")) u_R3 (
    .D(Clock), .Q(R3), .clk(demultiplexer_1_out3), .clr(Reset));  // open: en
  Register #(.width(16), .trigger("falling")) u_R4 (
    .D(Clock), .Q(R4), .clk(demultiplexer_1_out4), .clr(Reset));  // open: en
  Register #(.width(16), .trigger("falling")) R5 (
    .D(Clock), .Q(R0_2), .clk(demultiplexer_1_out5), .clr(Reset));  // open: en
  Register #(.width(16), .trigger("falling")) R6 (
    .D(Clock), .Q(Reset_2), .clk(demultiplexer_1_out6), .clr(Reset));  // open: en
  Register #(.width(16), .trigger("falling")) u_R7 (
    .D(Clock), .Q(R3_3), .clk(demultiplexer_1_out7), .clr(Reset));  // open: en
  Multiplexer #(.select(3), .width(16), .trigger("falling")) R5_2 (
    .in0(R0), .in1(R1_2), .in2(R2), .in3(R3), .in4(R4), .in5(R0_2), .in6(Reset_2), .in7(R3_3), .out(R1),
    .sel(SR1), .en(Clock_2));
  Multiplexer #(.select(3), .width(16), .trigger("falling")) u_R0_2 (
    .in0(R0), .in1(R1_2), .in2(R2), .in3(R3), .in4(R4), .in5(R0_2), .in6(Reset_2), .in7(R3_3), .out(OUT_SR2),
    .sel(SR2), .en(Clock_2));
  Multiplexer #(.select(3), .width(16)) multiplexer_1 (
    .in0(R0), .in1(R1_2), .in2(R2), .in3(R3), .in4(R4), .in5(R0_2), .in6(Reset_2), .in7(R3_3), .out(R3_2),
    .sel(DR), .en(Clock_2));

  assign R7 = Clock_2;
  assign WriteReg_2 = WriteReg;
endmodule

module RegPC (
  input  CTRL,
  input  CTRL_2,
  input  Cond,
  input  Clock,
  input  Clock_2,
  input  Reset,
  input  Reset_2,
  output [15:0] PC
);

  wire adder_1_cout, and_1_out, undriven_3, undriven_4;
  wire [15:0] adder_1_out, multiplexer_1_out, undriven, undriven_2;

  and and_1 (and_1_out, CTRL, Cond);
  Adder #(.width(16)) adder_1 (.a(PC), .b(undriven), .out(adder_1_out), .cin(undriven_3), .cout(adder_1_cout));
  Adder #(.width(16)) adder_2 (.a(PC), .b(undriven), .out(adder_1_out), .cin(undriven_3), .cout(adder_1_cout));
  Multiplexer #(.width(16), .enable("false")) multiplexer_1 (
    .in0(adder_1_out), .in1(undriven_2), .out(multiplexer_1_out), .sel(and_1_out));
  Register #(.width(16), .trigger("falling")) u_PC (
    .D(multiplexer_1_out), .en(undriven_4), .Q(PC), .clk(Clock), .clr(Reset));
  Register #(.width(16), .trigger("falling")) PC_2 (
    .D(multiplexer_1_out), .en(undriven_4), .Q(PC), .clk(Clock), .clr(Reset));

  assign Clock_2 = Clock;
  assign CTRL_2 = CTRL;
  assign Reset_2 = Reset;
endmodule

module Seq (
  input  ClockOrig,
  input  reset,
  output Fetch,
  output Exec
);

  wire not_1_out;

  Register #(.width(1), .trigger("falling")) register_1 (
    .D(not_1_out), .Q(Fetch), .clk(ClockOrig), .clr(reset));  // open: en
  not not_1 (not_1_out, Fetch);
  buf buffer_1 (Exec, ClockOrig);
  buf buffer_2 (Exec, ClockOrig);
endmodule

module _16_bit_transistor (
  input  [15:0] in_1,
  input  [15:0] in_2,
  input  Test,
  output [15:0] Arith
);

  wire undriven, undriven_2, undriven_3, undriven_4, undriven_5, undriven_6, undriven_7, undriven_8,
       undriven_9;

  and and_1 (Arith[2], undriven, Test);
  and and_2 (Arith[5], undriven_7, Test);
  and and_3 (Arith[5], undriven_7, Test);
  and and_4 (Arith[6], undriven_2, Test);
  and and_5 (Arith[7], undriven_8, Test);
  and and_6 (Arith[7], undriven_8, Test);
  and and_7 (Arith[8], undriven_3, Test);
  and and_8 (Arith[8], undriven_3, Test);
  and and_9 (Arith[10], undriven_9, Test);
  and and_10 (Arith[10], undriven_9, Test);
  and and_11 (Arith[12], undriven_4, Test);
  and and_12 (Arith[13], undriven_5, Test);
  and and_13 (Arith[13], undriven_5, Test);
  and and_14 (Arith[13], undriven_5, Test);
  and and_15 (Arith[14], undriven_6, Test);
  and and_16 (Arith[14], undriven_6, Test);
  and and_17 (Arith[14], undriven_6, Test);

  assign in_2 = in_1;
endmodule
